# Fritzing sketch arduino ampel (saved by Fritzing 0.9.3b)
breadboards: 1

parts:
  LED1 = LED - 5mm [color="Red (633nm)" package="5 mm [THT]"]  # not connected
  LED2 = LED - 5mm [color="Red (633nm)" package="5 mm [THT]"]
  Bauteil1 = Arduino Mega 2560 (Rev3)
  LED3 = Super Flux LED blue [color=Blue]
  LED4 = RGB LED (com. cathode, rbg) [package="5 mm [THT]"]

nets:
  N1: LED2.cathode, Bauteil1.GND, LED3.cathode, LED4.red_anode
  N2: Bauteil1.D2_PWM, LED3.anode

// code stored in the sketch: arduino ampel.ino
#define ABSTAND 500

//Ampel 1
#define ROT 2
#define GELB 1
#define GRUEN 0

//Ampel 2
#define ROT1 5
#define GELB1 4
#define GRUEN1 3
/*
//Ampel 3
#define ROT2 8
#define GELB2 7
#define GRUEN2 6

//Ampel 4
#define ROT3 11
#define GELB3 10
#define GRUEN3 9
*/

void setup() {
  //Ampel 1
  pinMode(ROT,OUTPUT);
  pinMode(GELB,OUTPUT);
  pinMode(GRUEN,OUTPUT);

  //Ampel 2
  pinMode(ROT1,OUTPUT);
  pinMode(GELB1,OUTPUT);
  pinMode(GRUEN1,OUTPUT);
/*
  //Ampel 3
  pinMode(ROT2,OUTPUT);
  pinMode(GELB2,OUTPUT);
  pinMode(GRUEN2,OUTPUT);

  //Ampel 4
  pinMode(ROT3,OUTPUT);
  pinMode(GELB3,OUTPUT);
  pinMode(GRUEN3,OUTPUT);
*/
}

void loop() {
  //Ampel 1
  digitalWrite(GRUEN,HIGH);
  delay(ABSTAND*10);
  digitalWrite(GRUEN,LOW);
  delay(ABSTAND);
  
  digitalWrite(GELB,HIGH);
  delay(ABSTAND);
  digitalWrite(GELB,LOW);
  delay(ABSTAND);

  digitalWrite(ROT,HIGH);
  delay(ABSTAND*10);
  digitalWrite(ROT,LOW);
  delay(ABSTAND);

  digitalWrite(GELB,HIGH);
  delay(ABSTAND);
  digitalWrite(GELB,LOW);
  delay(ABSTAND);


  //Ampel 2
  digitalWrite(GRUEN1,HIGH);
  delay(ABSTAND*10);
  digitalWrite(GRUEN1,LOW);
  delay(ABSTAND);
  
  digitalWrite(GELB1,HIGH);
  delay(ABSTAND);
  digitalWrite(GELB1,LOW);
  delay(ABSTAND);

  digitalWrite(ROT1,HIGH);
  delay(ABSTAND*10);
  digitalWrite(ROT1,LOW);
  delay(ABSTAND);

  digitalWrite(GELB1,HIGH);
  delay(ABSTAND);
  digitalWrite(GELB1,LOW);
  delay(ABSTAND);

/*
  //Ampel 3
  digitalWrite(GRUEN2,HIGH);
  delay(ABSTAND*10);
  digitalWrite(GRUEN2,LOW);
  delay(ABSTAND);
  
  digitalWrite(GELB2,HIGH);
  delay(ABSTAND);
  digitalWrite(GELB2,LOW);
  delay(ABSTAND);

  digitalWrite(ROT2,HIGH);
  delay(ABSTAND*10);
  digitalWrite(ROT2,LOW);
  delay(ABSTAND);

  digitalWrite(GELB2,HIGH);
  delay(ABSTAND);
  digitalWrite(GELB2,LOW);
  delay(ABSTAND);


  //Ampel 4
  digitalWrite(GRUEN3,HIGH);
  delay(ABSTAND*10);
  digitalWrite(GRUEN3,LOW);
  delay(ABSTAND);
  
  digitalWrite(GELB3,HIGH);
  delay(ABSTAND);
  digitalWrite(GELB3,LOW);
  delay(ABSTAND);

  digitalWrite(ROT3,HIGH);
  delay(ABSTAND*10);
  digitalWrite(ROT3,LOW);
  delay(ABSTAND);

  digitalWrite(GELB3,HIGH);
  delay(ABSTAND);
  digitalWrite(GELB3,LOW);
  delay(ABSTAND);
*/
}
