// Digital circuit 1_4_f.dig as structural Verilog
module _1_4_f (
  input  A,
  input  B,
  input  C,
  output out_4
);

  wire and_1_out, and_2_out, and_3_out, not_1_out, not_2_out, not_3_out;

  not not_1 (not_1_out, A);
  not not_2 (not_2_out, B);
  not not_3 (not_3_out, C);
  and and_1 (and_1_out, C, not_1_out, not_2_out);
  and and_2 (and_2_out, not_2_out, not_3_out, A);
  and and_3 (and_3_out, A, C);
  nand nand_1 (out_4, ~and_1_out, ~and_3_out, ~and_2_out);  // NAnd
endmodule
