// Digital circuit Aufgabe3.dig as structural Verilog
module Aufgabe3 (
  input  x3,
  input  x2,
  input  x1,
  input  x0,
  input  f,
  input  g
);

  wire abcde_1_a, abcde_1_b, abcde_1_c, abcde_1_d, abcde_1_e;

  abcde abcde_1 (
    .x0(x0), .x1(x1), .x2(x2), .x3(x3), .a(abcde_1_a), .b(abcde_1_b), .c(abcde_1_c), .d(abcde_1_d),
    .e(abcde_1_e));
  Seven_Seg seven_seg_1 (
    .a(abcde_1_a), .b(abcde_1_b), .c(abcde_1_c), .d(abcde_1_d), .e(abcde_1_e), .f(f), .g(g), .dp(1'b0));
endmodule
