// Digital circuit abcde.dig as structural Verilog
module abcde (
  input  x0,
  input  x1,
  input  x2,
  input  x3,
  output a,
  output b,
  output c,
  output d,
  output e
);

  Multiplexer #(.Selector_Bits(4)) multiplexer_1 (
    .sel({x3, x2, x1, x0}), .in_0(1'b1), .in_1(1'b0), .in_2(1'b1), .in_3(1'b1), .in_4(1'b0), .in_5(1'b1),
    .in_6(1'b1), .in_7(1'b1), .in_8(1'b1), .in_9(1'b1), .in_10(1'b0), .in_11(1'b0), .in_12(1'b0),
    .in_13(1'b0), .in_14(1'b0), .in_15(1'b0), .out(a));
  Multiplexer #(.Selector_Bits(4)) multiplexer_2 (
    .sel({x3, x2, x1, x0}), .in_0(1'b1), .in_1(1'b1), .in_2(1'b1), .in_3(1'b1), .in_4(1'b1), .in_5(1'b0),
    .in_6(1'b0), .in_7(1'b1), .in_8(1'b1), .in_9(1'b1), .in_10(1'b0), .in_11(1'b0), .in_12(1'b0),
    .in_13(1'b0), .in_14(1'b0), .in_15(1'b0), .out(b));
  Multiplexer #(.Selector_Bits(4)) multiplexer_3 (
    .sel({x3, x2, x1, x0}), .in_0(1'b1), .in_1(1'b1), .in_2(1'b0), .in_3(1'b1), .in_4(1'b1), .in_5(1'b1),
    .in_6(1'b1), .in_7(1'b1), .in_8(1'b1), .in_9(1'b1), .in_10(1'b0), .in_11(1'b0), .in_12(1'b0),
    .in_13(1'b0), .in_14(1'b0), .in_15(1'b0), .out(c));
  Multiplexer #(.Selector_Bits(4)) multiplexer_4 (
    .sel({x3, x2, x1, x0}), .in_0(1'b1), .in_1(1'b0), .in_2(1'b1), .in_3(1'b1), .in_4(1'b0), .in_5(1'b1),
    .in_6(1'b1), .in_7(1'b0), .in_8(1'b1), .in_9(1'b1), .in_10(1'b0), .in_11(1'b0), .in_12(1'b0),
    .in_13(1'b0), .in_14(1'b0), .in_15(1'b0), .out(d));
  Multiplexer #(.Selector_Bits(4)) multiplexer_5 (
    .sel({x3, x2, x1, x0}), .in_0(1'b1), .in_1(1'b0), .in_2(1'b1), .in_3(1'b0), .in_4(1'b0), .in_5(1'b0),
    .in_6(1'b1), .in_7(1'b0), .in_8(1'b1), .in_9(1'b0), .in_10(1'b0), .in_11(1'b0), .in_12(1'b0),
    .in_13(1'b0), .in_14(1'b0), .in_15(1'b0), .out(e));
endmodule
