// Digital circuit Schaltungssimulation-Aufgb.1.3.dig as structural Verilog
module Schaltungssimulation_Aufgb_1_3 (
  input  a,
  input  b,
  input  c
);

  wire and_1_out, and_2_out, and_3_out, and_4_out, nor_1_out, not_1_out, not_2_out, or_1_out;

  and and_1 (and_1_out, not_1_out, a);
  not not_1 (not_1_out, c);
  and and_2 (and_2_out, b, c);
  and and_3 (and_3_out, not_2_out, b);
  not not_2 (not_2_out, a);
  nor nor_1 (nor_1_out, and_1_out, and_2_out);
  or or_1 (or_1_out, and_2_out, and_3_out);
  and and_4 (and_4_out, nor_1_out, or_1_out);
  LED f (.in(and_4_out));
endmodule
