// Digital circuit ringshift-multiplexer.dig as structural Verilog
module ringshift_multiplexer (
  input  in_1,
  input  clk,
  input  in_3,
  input  in_4,
  input  in_5,
  input  [1:0] in_6,
  output out_7,
  output out_8,
  output out_9,
  output out_10
);

  wire multiplexer_1_out, multiplexer_2_out, multiplexer_3_out, multiplexer_4_out;

  Multiplexer #(.Selector_Bits(2)) multiplexer_1 (
    .sel(in_6), .in_0(in_1), .in_1(out_10), .in_2(out_8), .in_3(1'b0), .out(multiplexer_1_out));
  D_FF d_ff_1 (.D(multiplexer_1_out), .C(clk), .Q(out_7));  // open: nQ
  Multiplexer #(.Selector_Bits(2)) multiplexer_2 (
    .sel(in_6), .in_0(in_3), .in_1(out_7), .in_2(out_9), .in_3(1'b0), .out(multiplexer_2_out));
  D_FF d_ff_2 (.D(multiplexer_2_out), .C(clk), .Q(out_8));  // open: nQ
  Multiplexer #(.Selector_Bits(2)) multiplexer_3 (
    .sel(in_6), .in_0(in_4), .in_1(out_8), .in_2(out_10), .in_3(1'b0), .out(multiplexer_3_out));
  D_FF d_ff_3 (.D(multiplexer_3_out), .C(clk), .Q(out_9));  // open: nQ
  Multiplexer #(.Selector_Bits(2)) multiplexer_4 (
    .sel(in_6), .in_0(in_5), .in_1(out_9), .in_2(out_7), .in_3(1'b0), .out(multiplexer_4_out));
  D_FF d_ff_4 (.D(multiplexer_4_out), .C(clk), .Q(out_10));  // open: nQ
endmodule
