// Digital circuit d flipflop.dig as structural Verilog
module d_flipflop (
  input  D,
  input  CK,
  output Q,
  output nQ
);

  wire nand_1_out, nand_2_out;

  nand nand_1 (nand_1_out, D, CK);
  nand nand_2 (nand_2_out, nand_1_out, CK);
  nand nand_3 (Q, nand_1_out, nQ);
  nand nand_4 (nQ, Q, nand_2_out);
endmodule
