// Digital circuit multifunktionsschieberegister.dig as structural Verilog
module multifunktionsschieberegister (
  input  Clock,
  input  [1:0] Sel,
  input  D,
  input  D_2,
  input  D_3,
  input  D_4,
  input  D_5,
  input  D_6,
  input  D_7,
  input  D_8,
  output out_11,
  output out_12,
  output out_13,
  output out_14,
  output out_15,
  output out_16,
  output out_17,
  output out_18
);

  wire D0, D1, D2, D3, D4, D5, D6, D7;

  Multiplexer #(.Selector_Bits(2)) multiplexer_1 (
    .sel(Sel), .in_0(D), .in_1(out_16), .in_2(out_12), .in_3(1'b0), .out(D0));
  Multiplexer #(.Selector_Bits(2)) multiplexer_2 (
    .sel(Sel), .in_0(D_2), .in_1(out_11), .in_2(out_13), .in_3(1'b0), .out(D1));
  Multiplexer #(.Selector_Bits(2)) multiplexer_3 (
    .sel(Sel), .in_0(D_3), .in_1(out_12), .in_2(out_14), .in_3(1'b0), .out(D2));
  Multiplexer #(.Selector_Bits(2)) multiplexer_4 (
    .sel(Sel), .in_0(D_4), .in_1(out_13), .in_2(out_17), .in_3(1'b0), .out(D3));
  Multiplexer #(.Selector_Bits(2)) multiplexer_5 (
    .sel(Sel), .in_0(D_5), .in_1(out_14), .in_2(out_15), .in_3(1'b0), .out(D4));
  Multiplexer #(.Selector_Bits(2)) multiplexer_6 (
    .sel(Sel), .in_0(D_6), .in_1(out_17), .in_2(out_18), .in_3(1'b0), .out(D5));
  Multiplexer #(.Selector_Bits(2)) multiplexer_7 (
    .sel(Sel), .in_0(D_7), .in_1(out_15), .in_2(out_16), .in_3(1'b0), .out(D6));
  Multiplexer #(.Selector_Bits(2)) multiplexer_8 (
    .sel(Sel), .in_0(D_8), .in_1(out_18), .in_2(out_11), .in_3(1'b0), .out(D7));
  parallel_shift_register parallel_shift_register_1 (
    .D0(D0), .D1(D1), .D2(D2), .D3(D3), .D4(D4), .D5(D5), .D6(D6), .D7(D7), .CK(Clock), .Q7(out_16),
    .Q6(out_18), .Q5(out_15), .Q4(out_17), .Q3(out_14), .Q2(out_13), .Q1(out_12), .Q0(out_11));

  // Other names for the same wires on the sheet: LS0 = out_11; LS1 = out_12; LS2 = out_13; LS3 = out_14; LS4 = out_17;
  //   LS5 = out_15; LS6 = out_18; LS7 = out_16

  // Notes on the sheet:
  //   Clock: Hz: 500
endmodule
