// Digital circuit parallel shift register.dig as structural Verilog
module parallel_shift_register (
  input  D0,
  input  D1,
  input  D2,
  input  D3,
  input  D4,
  input  D5,
  input  D6,
  input  D7,
  input  CK,
  output Q7,
  output Q6,
  output Q5,
  output Q4,
  output Q3,
  output Q2,
  output Q1,
  output Q0
);

  D_FF d_ff_1 (.D(D0), .C(CK), .Q(Q0));  // open: nQ
  D_FF d_ff_2 (.D(D1), .C(CK), .Q(Q1));  // open: nQ
  D_FF d_ff_3 (.D(D2), .C(CK), .Q(Q2));  // open: nQ
  D_FF d_ff_4 (.D(D3), .C(CK), .Q(Q3));  // open: nQ
  D_FF d_ff_5 (.D(D4), .C(CK), .Q(Q4));  // open: nQ
  D_FF d_ff_6 (.D(D5), .C(CK), .Q(Q5));  // open: nQ
  D_FF d_ff_7 (.D(D6), .C(CK), .Q(Q6));  // open: nQ
  D_FF d_ff_8 (.D(D7), .C(CK), .Q(Q7));  // open: nQ
endmodule
