// Digital circuit 1_1_b_dmf.dig as structural Verilog
module _1_1_b_dmf (
  input  A,
  input  B,
  input  C,
  input  D,
  output Y
);

  wire and_1_out, and_2_out, and_3_out;

  and and_1 (and_1_out, A, B, D);
  and and_2 (and_2_out, ~B, ~D);  // And
  and and_3 (and_3_out, ~C, D);  // And
  or or_1 (Y, and_1_out, and_2_out, and_3_out);
endmodule
