// Digital circuit 1_1_b_kmf.dig as structural Verilog
module _1_1_b_kmf (
  input  A,
  input  B,
  input  C,
  input  D,
  output Y
);

  wire or_1_out, or_2_out, or_3_out;

  or or_1 (or_1_out, A, ~B, ~C);  // Or
  or or_2 (or_2_out, ~B, D);  // Or
  or or_3 (or_3_out, B, ~C, ~D);  // Or
  and and_1 (Y, or_1_out, or_2_out, or_3_out);
endmodule
