// Digital circuit 4_1_b_halbaddierer.dig as structural Verilog
module _4_1_b_halbaddierer (
  input  A,
  input  B,
  output S,
  output C
);

  wire or_1_out;

  and and_1 (C, A, B);
  or or_1 (or_1_out, A, B);
  and and_2 (S, ~C, or_1_out);  // And
endmodule
