// Digital circuit 4_1_c_volladdierer.dig as structural Verilog
module _4_1_c_volladdierer (
  input  A,
  input  B,
  input  C,
  output S,
  output C1
);

  wire _4_1_b_halbaddierer_1_c, _4_1_b_halbaddierer_1_s, _4_1_b_halbaddierer_2_c;

  _4_1_b_halbaddierer _4_1_b_halbaddierer_1 (.A(A), .B(B), .S(_4_1_b_halbaddierer_1_s), .C(_4_1_b_halbaddierer_1_c));
  _4_1_b_halbaddierer _4_1_b_halbaddierer_2 (.A(C), .B(_4_1_b_halbaddierer_1_s), .S(S), .C(_4_1_b_halbaddierer_2_c));
  or or_1 (C1, _4_1_b_halbaddierer_2_c, _4_1_b_halbaddierer_1_c);
endmodule
