// Digital circuit 4_1_d_16bit_addierer.dig as structural Verilog
module _4_1_d_16bit_addierer (
  input  B1,
  input  A1,
  input  B2,
  input  A2,
  input  B4,
  input  A4,
  input  B8,
  input  A8,
  input  B16,
  input  A16,
  input  B32,
  input  A32,
  input  B64,
  input  A64,
  input  B128,
  input  A128,
  input  B256,
  input  A256,
  input  B512,
  input  A512,
  input  B1024,
  input  A1024,
  input  B2048,
  input  A2048,
  input  B4096,
  input  A4096,
  input  B8192,
  input  A8192,
  input  B16384,
  input  A16384,
  input  B32768,
  input  A32768,
  output C1,
  output C2,
  output C4,
  output C8,
  output C16,
  output C32,
  output C64,
  output C128,
  output C256,
  output C512,
  output C1024,
  output C2048,
  output C4096,
  output C8192,
  output C16384,
  output C32768,
  output C65536
);

  wire _4_1_c_volladdierer_2_c1, _4_1_c_volladdierer_3_c1, _4_1_c_volladdierer_4_c1,
       _4_1_c_volladdierer_5_c1, _4_1_c_volladdierer_6_c1, _4_1_c_volladdierer_7_c1,
       _4_1_c_volladdierer_8_c1, _4_1_c_volladdierer_9_c1, _4_1_c_volladdierer_10_c1,
       _4_1_c_volladdierer_11_c1, _4_1_c_volladdierer_12_c1, _4_1_c_volladdierer_13_c1,
       _4_1_c_volladdierer_14_c1, _4_1_c_volladdierer_15_c1, _4_1_c_volladdierer_16_c1;

  _4_1_c_volladdierer _4_1_c_volladdierer_1 (
    .A(B32768), .B(A32768), .C(_4_1_c_volladdierer_2_c1), .S(C32768), .C1(C65536));
  _4_1_c_volladdierer _4_1_c_volladdierer_2 (
    .A(B16384), .B(A16384), .C(_4_1_c_volladdierer_3_c1), .S(C16384), .C1(_4_1_c_volladdierer_2_c1));
  _4_1_c_volladdierer _4_1_c_volladdierer_3 (
    .A(B8192), .B(A8192), .C(_4_1_c_volladdierer_4_c1), .S(C8192), .C1(_4_1_c_volladdierer_3_c1));
  _4_1_c_volladdierer _4_1_c_volladdierer_4 (
    .A(B4096), .B(A4096), .C(_4_1_c_volladdierer_5_c1), .S(C4096), .C1(_4_1_c_volladdierer_4_c1));
  _4_1_c_volladdierer _4_1_c_volladdierer_5 (
    .A(B2048), .B(A2048), .C(_4_1_c_volladdierer_6_c1), .S(C2048), .C1(_4_1_c_volladdierer_5_c1));
  _4_1_c_volladdierer _4_1_c_volladdierer_6 (
    .A(B1024), .B(A1024), .C(_4_1_c_volladdierer_7_c1), .S(C1024), .C1(_4_1_c_volladdierer_6_c1));
  _4_1_c_volladdierer _4_1_c_volladdierer_7 (
    .A(B512), .B(A512), .C(_4_1_c_volladdierer_8_c1), .S(C512), .C1(_4_1_c_volladdierer_7_c1));
  _4_1_c_volladdierer _4_1_c_volladdierer_8 (
    .A(B256), .B(A256), .C(_4_1_c_volladdierer_9_c1), .S(C256), .C1(_4_1_c_volladdierer_8_c1));
  _4_1_c_volladdierer _4_1_c_volladdierer_9 (
    .A(B128), .B(A128), .C(_4_1_c_volladdierer_10_c1), .S(C128), .C1(_4_1_c_volladdierer_9_c1));
  _4_1_c_volladdierer _4_1_c_volladdierer_10 (
    .A(B64), .B(A64), .C(_4_1_c_volladdierer_11_c1), .S(C64), .C1(_4_1_c_volladdierer_10_c1));
  _4_1_c_volladdierer _4_1_c_volladdierer_11 (
    .A(B32), .B(A32), .C(_4_1_c_volladdierer_12_c1), .S(C32), .C1(_4_1_c_volladdierer_11_c1));
  _4_1_c_volladdierer _4_1_c_volladdierer_12 (
    .A(B16), .B(A16), .C(_4_1_c_volladdierer_13_c1), .S(C16), .C1(_4_1_c_volladdierer_12_c1));
  _4_1_c_volladdierer _4_1_c_volladdierer_13 (
    .A(B8), .B(A8), .C(_4_1_c_volladdierer_14_c1), .S(C8), .C1(_4_1_c_volladdierer_13_c1));
  _4_1_c_volladdierer _4_1_c_volladdierer_14 (
    .A(B4), .B(A4), .C(_4_1_c_volladdierer_15_c1), .S(C4), .C1(_4_1_c_volladdierer_14_c1));
  _4_1_c_volladdierer _4_1_c_volladdierer_15 (
    .A(B2), .B(A2), .C(_4_1_c_volladdierer_16_c1), .S(C2), .C1(_4_1_c_volladdierer_15_c1));
  _4_1_c_volladdierer _4_1_c_volladdierer_16 (.A(B1), .B(A1), .C(1'b0), .S(C1), .C1(_4_1_c_volladdierer_16_c1));
endmodule
