// Digital circuit 4_1_d_16bit_addierer_bus.dig as structural Verilog
module _4_1_d_16bit_addierer_bus (
  input  [15:0] A,
  input  [15:0] B,
  input  Ci,
  output [15:0] S,
  output C0
);

  wire _4_1_c_volladdierer_2_c1, _4_1_c_volladdierer_3_c1, _4_1_c_volladdierer_4_c1,
       _4_1_c_volladdierer_5_c1, _4_1_c_volladdierer_6_c1, _4_1_c_volladdierer_7_c1,
       _4_1_c_volladdierer_8_c1, _4_1_c_volladdierer_9_c1, _4_1_c_volladdierer_10_c1,
       _4_1_c_volladdierer_11_c1, _4_1_c_volladdierer_12_c1, _4_1_c_volladdierer_13_c1,
       _4_1_c_volladdierer_14_c1, _4_1_c_volladdierer_15_c1, _4_1_c_volladdierer_16_c1;

  _4_1_c_volladdierer _4_1_c_volladdierer_1 (.A(B[15]), .B(A[15]), .C(_4_1_c_volladdierer_2_c1), .S(S[15]), .C1(C0));
  _4_1_c_volladdierer _4_1_c_volladdierer_2 (
    .A(B[14]), .B(A[14]), .C(_4_1_c_volladdierer_3_c1), .S(S[14]), .C1(_4_1_c_volladdierer_2_c1));
  _4_1_c_volladdierer _4_1_c_volladdierer_3 (
    .A(B[13]), .B(A[13]), .C(_4_1_c_volladdierer_4_c1), .S(S[13]), .C1(_4_1_c_volladdierer_3_c1));
  _4_1_c_volladdierer _4_1_c_volladdierer_4 (
    .A(B[12]), .B(A[12]), .C(_4_1_c_volladdierer_5_c1), .S(S[12]), .C1(_4_1_c_volladdierer_4_c1));
  _4_1_c_volladdierer _4_1_c_volladdierer_5 (
    .A(B[11]), .B(A[11]), .C(_4_1_c_volladdierer_6_c1), .S(S[11]), .C1(_4_1_c_volladdierer_5_c1));
  _4_1_c_volladdierer _4_1_c_volladdierer_6 (
    .A(B[10]), .B(A[10]), .C(_4_1_c_volladdierer_7_c1), .S(S[10]), .C1(_4_1_c_volladdierer_6_c1));
  _4_1_c_volladdierer _4_1_c_volladdierer_7 (
    .A(B[9]), .B(A[9]), .C(_4_1_c_volladdierer_8_c1), .S(S[9]), .C1(_4_1_c_volladdierer_7_c1));
  _4_1_c_volladdierer _4_1_c_volladdierer_8 (
    .A(B[8]), .B(A[8]), .C(_4_1_c_volladdierer_9_c1), .S(S[8]), .C1(_4_1_c_volladdierer_8_c1));
  _4_1_c_volladdierer _4_1_c_volladdierer_9 (
    .A(B[7]), .B(A[7]), .C(_4_1_c_volladdierer_10_c1), .S(S[7]), .C1(_4_1_c_volladdierer_9_c1));
  _4_1_c_volladdierer _4_1_c_volladdierer_10 (
    .A(B[6]), .B(A[6]), .C(_4_1_c_volladdierer_11_c1), .S(S[6]), .C1(_4_1_c_volladdierer_10_c1));
  _4_1_c_volladdierer _4_1_c_volladdierer_11 (
    .A(B[5]), .B(A[5]), .C(_4_1_c_volladdierer_12_c1), .S(S[5]), .C1(_4_1_c_volladdierer_11_c1));
  _4_1_c_volladdierer _4_1_c_volladdierer_12 (
    .A(B[4]), .B(A[4]), .C(_4_1_c_volladdierer_13_c1), .S(S[4]), .C1(_4_1_c_volladdierer_12_c1));
  _4_1_c_volladdierer _4_1_c_volladdierer_13 (
    .A(B[3]), .B(A[3]), .C(_4_1_c_volladdierer_14_c1), .S(S[3]), .C1(_4_1_c_volladdierer_13_c1));
  _4_1_c_volladdierer _4_1_c_volladdierer_14 (
    .A(B[2]), .B(A[2]), .C(_4_1_c_volladdierer_15_c1), .S(S[2]), .C1(_4_1_c_volladdierer_14_c1));
  _4_1_c_volladdierer _4_1_c_volladdierer_15 (
    .A(B[1]), .B(A[1]), .C(_4_1_c_volladdierer_16_c1), .S(S[1]), .C1(_4_1_c_volladdierer_15_c1));
  _4_1_c_volladdierer _4_1_c_volladdierer_16 (.A(B[0]), .B(A[0]), .C(Ci), .S(S[0]), .C1(_4_1_c_volladdierer_16_c1));

  // Other names for the same wires on the sheet: A1 = A[0]; A2 = A[1]; A3 = A[2]; A4 = A[3]; A5 = A[4]; A6 = A[5];
  //   A7 = A[6]; A8 = A[7]; A9 = A[8]; A10 = A[9]; A11 = A[10]; A12 = A[11]; A13 = A[12]; A14 = A[13]; A15 = A[14];
  //   A16 = A[15]; B1 = B[0]; B2 = B[1]; B3 = B[2]; B4 = B[3]; B5 = B[4]; B6 = B[5]; B7 = B[6]; B8 = B[7]; B9 = B[8];
  //   B10 = B[9]; B11 = B[10]; B12 = B[11]; B13 = B[12]; B14 = B[13]; B15 = B[14]; B16 = B[15]; C1 = S[0]; C2 = S[1];
  //   C3 = S[2]; C4 = S[3]; C5 = S[4]; C6 = S[5]; C7 = S[6]; C8 = S[7]; C9 = S[8]; C10 = S[9]; C11 = S[10];
  //   C12 = S[11]; C13 = S[12]; C14 = S[13]; C15 = S[14]; C16 = S[15]; C17 = C0
endmodule
