// Digital circuit 4_1_f_alu.dig as structural Verilog
module _4_1_f_alu (
  input  [15:0] A,
  input  [15:0] B,
  input  [1:0] S,
  output [15:0] Y
);

  wire [15:0] _4_1_e_ringshift_1_y, add_1_s, and_1_out, not_1_out;

  Add #(.Bits(16)) add_1 (.a(A), .b(B), .c_i(1'b0), .s(add_1_s));  // open: c_o
  assign and_1_out = A & B;  // And and_1, 16 bits wide
  assign not_1_out = ~A;  // Not not_1, 16 bits wide
  _4_1_e_ringshift _4_1_e_ringshift_1 (.A(A), .Y(_4_1_e_ringshift_1_y));
  Multiplexer #(.Bits(16), .Selector_Bits(2)) multiplexer_1 (
    .sel(S), .in_0(add_1_s), .in_1(and_1_out), .in_2(not_1_out), .in_3(_4_1_e_ringshift_1_y), .out(Y));
endmodule
