// Digital circuit Übung6-nand-ffs.dig as structural Verilog
module \Übung6_nand_ffs  (
  input  S,
  input  R,
  input  clk,
  input  notS,
  input  notR,
  input  J,
  input  K,
  input  clk_2,
  output Q,
  output notQ,
  output Q_2,
  output notQ_2,
  output Q_3,
  output notQ_3
);

  wire and_1_out, delay_1_out, nand_1_out, nand_2_out, nand_3_out, nand_4_out, not_1_out;

  Delay delay_1 (.in(clk_2), .out(delay_1_out));
  not not_1 (not_1_out, delay_1_out);
  and and_1 (and_1_out, clk_2, not_1_out);
  nand nand_1 (nand_1_out, S, clk);
  nand nand_2 (nand_2_out, clk, R);
  nand nand_3 (nand_3_out, notQ_3, J, and_1_out);
  nand nand_4 (nand_4_out, and_1_out, K, Q_3);
  nand nand_5 (Q_2, notS, notQ_2);
  nand nand_6 (notQ_2, Q_2, notR);
  nand nand_7 (Q, nand_1_out, notQ);
  nand nand_8 (notQ, Q, nand_2_out);
  nand nand_9 (Q_3, nand_3_out, notQ_3);
  nand nand_10 (notQ_3, Q_3, nand_4_out);
endmodule
